// Logisim project ligarDisplay.circ as structural Verilog: 1 circuit, main circuit main
module main (
);

  wire a_out, and_1_out, and_2_out, and_3_out, and_4_out, and_5_out, and_6_out, and_7_out, and_8_out,
       and_9_out, b_out, c_out, d_out, not_1_out, not_2_out, not_3_out, not_4_out, not_5_out, not_6_out,
       not_7_out, not_8_out, not_9_out, not_10_out, not_11_out, or_1_out, or_2_out, or_3_out, or_4_out,
       or_5_out, or_6_out, or_7_out, or_8_out;

  Button d (.out(d_out));
  Button c (.out(c_out));
  Button a (.out(a_out));
  Button b (.out(b_out));
  not not_1 (not_1_out, a_out);
  and and_1 (and_1_out, not_1_out, not_2_out);
  not not_2 (not_2_out, c_out);
  and and_2 (and_2_out, a_out, c_out);
  not not_3 (not_3_out, b_out);
  not not_4 (not_4_out, a_out);
  not not_5 (not_5_out, d_out);
  not not_6 (not_6_out, a_out);
  not not_7 (not_7_out, b_out);
  not not_8 (not_8_out, b_out);
  not not_9 (not_9_out, a_out);
  and and_3 (and_3_out, not_3_out, not_4_out);
  and and_4 (and_4_out, b_out, a_out);
  and and_5 (and_5_out, not_5_out, b_out);
  and and_6 (and_6_out, b_out, not_6_out);
  and and_7 (and_7_out, c_out, not_7_out, a_out);
  and and_8 (and_8_out, c_out, not_8_out);
  and and_9 (and_9_out, c_out, not_9_out);
  or or_1 (or_1_out, and_1_out, and_5_out, and_6_out, and_7_out);
  not not_10 (not_10_out, c_out);
  not not_11 (not_11_out, b_out);
  or or_2 (or_2_out, d_out, b_out, and_1_out, and_2_out);
  or or_3 (or_3_out, not_10_out, and_3_out, and_4_out);
  or or_4 (or_4_out, c_out, not_11_out, a_out);
  or or_5 (or_5_out, d_out, or_1_out);
  or or_6 (or_6_out, and_1_out, and_6_out);
  or or_7 (or_7_out, and_3_out, and_8_out, and_9_out, d_out);
  or or_8 (or_8_out, and_8_out, and_9_out, and_5_out, d_out);
  Button a_2 (.out(or_2_out));
  Button b_2 (.out(or_3_out));
  Button c_2 (.out(or_4_out));
  Button d_2 (.out(or_5_out));
  Button e (.out(or_6_out));
  Button f (.out(or_7_out));
  Button g (.out(or_8_out));
endmodule
